# Fritzing sketch NanoLoggerPluvio (saved by Fritzing 1.0.3b)
circuit board: 10cm x 5.2cm
breadboards: 1

parts:
  Nano = Arduino Nano (Rev3.0)
  RTC1307 = Adafruit PCF8523 RTC [part_number="Adafruit #3295"]
  SD = female pin header, 7 pins [form="♀ (female)"]
  Power = Screw terminal - 2 pins [package=THT]
  Pluvio = Screw terminal - 2 pins [package=THT]

nets:
  GND: Nano.GND, RTC1307.GND, SD.pin1, Power.pin2, Pluvio.pin2
  N1: Nano.D2, Pluvio.pin1
  N2: Nano.D3, SD.pin3
  N3: Nano.D10, SD.pin7
  N4: Nano.D11/MOSI, SD.pin6
  N5: Nano.D12/MISO, SD.pin4
  5V: Nano.5V, Nano.A0, RTC1307.VCC, SD.pin2, Power.pin1
  N6: Nano.A5, RTC1307.SCL
  N7: Nano.A4, RTC1307.SDA
  N8: Nano.D13/SCK, SD.pin5

notes:
  +
  -

custom parts:
  Adafruit PCF8523 RTC: This is a great battery-backed real time clock (RTC) that allows your microcontroller project to keep track of time even if it is reprogrammed, or if the power is lost. Perfect for datalogging, clock-building, time stamping, timers and alarms, etc. Equipped with PCF8523 RTC - it can run from 3.3V or 5V power & logic! Works great with an Arduino using our RTC library, with CircuitPython or with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
